// Logisim project 4Bitfulladder.circ as structural Verilog: 1 circuit, main circuit main
module main (
  input  A,
  input  B,
  input  C,
  output out_4,
  output out_5
);

  wire and_1_out, and_2_out, n7408_1_pin3, n7408_1_pin6, n7486_1_pin3, or_1_out, xor_1_out, xor_2_out;

  _7486 u_7486_1 (
    .pin1(A), .pin2(B), .pin3(n7486_1_pin3), .pin4(n7486_1_pin3), .pin5(C), .pin6(out_5));  // open: pin13, pin12, pin11, pin10, pin9, pin8
  xor xor_1 (xor_1_out, A, B);
  and and_1 (and_1_out, A, B);
  _7408 u_7408_1 (
    .pin1(A), .pin2(B), .pin3(n7408_1_pin3), .pin4(n7486_1_pin3), .pin5(C), .pin6(n7408_1_pin6));  // open: pin13, pin12, pin11, pin10, pin9, pin8
  xor xor_2 (xor_2_out, xor_1_out, C);
  // _7432 7432_1: pin names not known; wires that end beside it: 1'b1, n7408_1_pin3, n7408_1_pin6, out_4, 1'b0
  and and_2 (and_2_out, xor_1_out, C);
  LED led_1 (.in(xor_2_out));
  or or_1 (or_1_out, and_2_out, and_1_out);
  LED led_2 (.in(or_1_out));

  // Notes on the sheet:
  //   X-OR
  //   4 Bit Full Adder
  //   AND
  //   OR
endmodule
