// Logisim project 4b_full_adder_74283.circ as structural Verilog: 1 circuit, main circuit main
module main (
  input  A1,
  input  A2,
  input  A3,
  input  A4,
  input  B1,
  input  B2,
  input  B3,
  input  B4,
  input  Cin
);

  wire n74283_1_pin1, n74283_1_pin4, n74283_1_pin9, n74283_1_pin10, n74283_1_pin13;

  _74283 u_74283_1 (
    .pin1(n74283_1_pin1), .pin2(B2), .pin3(A2), .pin4(n74283_1_pin4), .pin5(A1), .pin6(B1), .pin7(Cin),
    .pin15(B3), .pin14(A3), .pin13(n74283_1_pin13), .pin12(A4), .pin11(B4), .pin10(n74283_1_pin10),
    .pin9(n74283_1_pin9));
  LED S1 (.in(n74283_1_pin4));
  LED S2 (.in(n74283_1_pin1));
  LED S3 (.in(n74283_1_pin13));
  LED S4 (.in(n74283_1_pin10));
  LED C0 (.in(n74283_1_pin9));
endmodule
