// Logisim project BCDAdders.circ as structural Verilog: 1 circuit, main circuit main
module main (
  input  A3,
  input  A2,
  input  A1,
  input  A0,
  input  B3,
  input  B2,
  input  B1,
  input  B0,
  input  in_9,
  input  in_10,
  input  in_11,
  input  in_12,
  input  in_13,
  input  in_14,
  input  in_15
);

  wire adder_1_cout, adder_2_cout, adder_3_cout, adder_4_cout, adder_5_cout, adder_6_cout, adder_7_cout,
       adder_8_cout, and_1_out, and_2_out, or_2_out;
  wire [7:0] adder_1_out, adder_2_out, adder_3_out, adder_4_out, adder_5_out, adder_6_out, adder_7_out,
       adder_8_out, or_1_out;
  wire [7:1] undriven, undriven_2;

  or or_1 (or_1_out[0], and_1_out, adder_2_cout, and_2_out);
  and and_1 (and_1_out, adder_2_out[0], adder_5_out[0]);
  and and_2 (and_2_out, adder_2_out[0], adder_3_out[0]);
  or or_2 (or_2_out, adder_2_cout, adder_1_cout);
  Adder adder_1 (.a(adder_2_out), .b({undriven, in_9}), .out(adder_1_out), .cin(adder_4_cout), .cout(adder_1_cout));
  Adder adder_2 (.out(adder_2_out), .cin(adder_3_cout), .cout(adder_2_cout));  // open: a, b
  Adder adder_3 (.out(adder_3_out), .cin(adder_5_cout), .cout(adder_3_cout));  // open: a, b
  Adder adder_4 (.a(adder_3_out), .b(or_1_out), .out(adder_4_out), .cin(adder_6_cout), .cout(adder_4_cout));
  Adder adder_5 (.out(adder_5_out), .cin(adder_7_cout), .cout(adder_5_cout));  // open: a, b
  Adder adder_6 (.a(adder_5_out), .b(or_1_out), .out(adder_6_out), .cin(adder_8_cout), .cout(adder_6_cout));
  Adder adder_7 (.out(adder_7_out), .cout(adder_7_cout));  // open: a, b, cin
  Adder adder_8 (.a(adder_7_out), .b({undriven_2, in_10}), .out(adder_8_out), .cout(adder_8_cout));  // open: cin
  // Pins of 1 and 8 bits meet at {undriven, in_9}
  // Pins of 1 and 8 bits meet at {undriven_2, in_10}
  // Pins of 1 and 8 bits meet at or_1_out
  // Pins of 1 and 8 bits meet at adder_2_out
  // Pins of 1 and 8 bits meet at adder_5_out
  // Pins of 1 and 8 bits meet at adder_3_out

  // Notes on the sheet:
  //   K
  //   Z8
  //   Z4
  //   Z2
  //   Z1
endmodule
