// Logisim project BCDAddersICCC.circ as structural Verilog: 2 circuits, main circuit main
module main (
  input  in_1,
  input  in_2,
  input  in_3,
  input  in_4,
  input  in_5,
  input  in_6,
  input  in_7,
  input  in_8,
  output out_9,
  output out_10,
  output out_11,
  output out_12,
  output out_13
);

  bcd bcd_1 (
    .A3(in_1), .A2(in_2), .A1(in_3), .A0(in_4), .B3(in_5), .B2(in_6), .B1(in_7), .B0(in_8), .out_11(out_9),
    .out_12(out_10), .out_13(out_11), .out_14(out_12), .out_15(out_13));  // open: in_9, in_10
endmodule

module bcd (
  input  A3,
  input  A2,
  input  A1,
  input  A0,
  input  B3,
  input  B2,
  input  B1,
  input  B0,
  input  in_9,
  input  in_10,
  output out_11,
  output out_12,
  output out_13,
  output out_14,
  output out_15
);

  wire adder_1_cout, adder_1_out, adder_2_cout, adder_3_cout, adder_3_out, adder_4_cout, adder_5_cout,
       adder_5_out, adder_6_cout, adder_7_cout, adder_7_out, adder_8_cout, and_1_out, and_2_out, or_1_out;

  or or_1 (or_1_out, and_1_out, adder_1_cout, and_2_out);
  and and_1 (and_1_out, adder_1_out, adder_5_out);
  and and_2 (and_2_out, adder_1_out, adder_3_out);
  or or_2 (out_15, adder_1_cout, adder_2_cout);
  Adder #(.width(1)) adder_1 (.a(A3), .b(B3), .out(adder_1_out), .cin(adder_3_cout), .cout(adder_1_cout));
  Adder #(.width(1)) adder_2 (.a(adder_1_out), .b(in_9), .out(out_14), .cin(adder_4_cout), .cout(adder_2_cout));
  Adder #(.width(1)) adder_3 (.a(A2), .b(B2), .out(adder_3_out), .cin(adder_5_cout), .cout(adder_3_cout));
  Adder #(.width(1)) adder_4 (.a(adder_3_out), .b(or_1_out), .out(out_11), .cin(adder_6_cout), .cout(adder_4_cout));
  Adder #(.width(1)) adder_5 (.a(A1), .b(B1), .out(adder_5_out), .cin(adder_7_cout), .cout(adder_5_cout));
  Adder #(.width(1)) adder_6 (.a(adder_5_out), .b(or_1_out), .out(out_12), .cin(adder_8_cout), .cout(adder_6_cout));
  Adder #(.width(1)) adder_7 (.a(A0), .b(B0), .out(adder_7_out), .cout(adder_7_cout));  // open: cin
  Adder #(.width(1)) adder_8 (.a(adder_7_out), .b(in_10), .out(out_13), .cout(adder_8_cout));  // open: cin
endmodule
