// Logisim project Comparator...circ as structural Verilog: 1 circuit, main circuit main
module main (
  input  in_1,
  input  in_2,
  input  in_3,
  input  in_4,
  input  in_5,
  input  in_6,
  input  in_7,
  input  in_8,
  input  in_9,
  input  in_10,
  input  in_11,
  input  in_12,
  input  in_13,
  input  in_14,
  input  in_15,
  input  in_16,
  input  in_17,
  input  in_18,
  input  in_19,
  input  in_20,
  input  in_21,
  input  in_22,
  input  in_23,
  input  in_24,
  input  in_25,
  input  in_26,
  input  in_27,
  input  in_28,
  input  in_29,
  output out_30,
  output out_31,
  output out_32
);

  wire and_1_out, and_2_out, and_3_out, and_4_out, and_5_out, and_6_out, and_7_out, and_8_out, xor_1_out,
       xor_2_out, xor_3_out, xor_4_out;

  xor xor_1 (xor_1_out, in_11, in_12);
  xor xor_2 (xor_2_out, in_13, in_14);
  xor xor_3 (xor_3_out, in_15, in_16);
  xor xor_4 (xor_4_out, in_17, in_18);
  and and_1 (and_1_out, in_1, in_2);
  and and_2 (and_2_out, in_3, in_8, in_4);
  and and_3 (and_3_out, in_5, in_9, in_6);
  and and_4 (and_4_out, in_7, in_8, in_9, in_28, in_10);
  and and_5 (and_5_out, in_19, in_20);
  and and_6 (and_6_out, in_21, in_22, in_23);
  and and_7 (and_7_out, in_24, in_25, in_22, in_27);
  and and_8 (and_8_out, in_28, in_28, in_9, in_22, in_29);
  and and_9 (out_31, xor_1_out, xor_2_out, xor_3_out, xor_4_out);
  or or_1 (out_30, and_1_out, and_2_out, and_3_out, and_4_out);
  or or_2 (out_32, and_5_out, and_6_out, and_7_out, and_8_out);

  assign in_26 = in_22;

  // Notes on the sheet:
  //   A>B
  //   A=B
  //   A<B
endmodule
