// Logisim project DeMultiplexerr.circ as structural Verilog
module DeMux (
  input  E,
  input  A,
  input  B,
  input  C,
  output [7:0] D
);

  wire not_1_out, not_2_out, not_3_out;

  not not_1 (not_1_out, A);
  not not_2 (not_2_out, B);
  not not_3 (not_3_out, C);
  and and_1 (D[7], E, not_1_out, not_2_out, not_3_out);
  and and_2 (D[6], E, not_1_out, not_2_out, C);
  and and_3 (D[5], E, not_1_out, B, not_3_out);
  and and_4 (D[4], E, not_1_out, B, C);
  and and_5 (D[3], E, A, not_2_out, not_3_out);
  and and_6 (D[2], E, A, not_2_out, C);
  and and_7 (D[1], E, A, B, not_3_out);
  and and_8 (D[0], E, A, B, C);

  // Notes on the sheet:
  //   D0,D1,D2,D3,D4,D5,D6,D7
endmodule
