// Logisim project Full_adder.circ as structural Verilog: 1 circuit, main circuit main
module main (
  input  in_1,
  input  in_2,
  input  in_3
);

  wire and_1_out, and_2_out, n7408_1_pin3, n7408_1_pin6, n7432_1_p4, n7486_1_pin3, n7486_1_pin6, or_1_out,
       undriven, xor_1_out, xor_2_out;

  xor xor_1 (xor_1_out, in_1, in_2);
  and and_1 (and_1_out, in_2, in_1);
  _7486 u_7486_1 (
    .pin1(in_1), .pin2(in_2), .pin3(n7486_1_pin3), .pin4(n7486_1_pin3), .pin5(in_3), .pin6(n7486_1_pin6));  // open: pin13, pin12, pin11, pin10, pin9, pin8
  xor xor_2 (xor_2_out, xor_1_out, in_3);
  and and_2 (and_2_out, in_3, xor_1_out);
  _7408 u_7408_1 (
    .pin1(n7486_1_pin3), .pin2(in_3), .pin3(n7408_1_pin3), .pin4(in_1), .pin5(in_2), .pin6(n7408_1_pin6));  // open: pin13, pin12, pin11, pin10, pin9, pin8
  LED led_1 (.in(n7486_1_pin6));
  or or_1 (or_1_out, and_2_out, and_1_out);
  // _7432 7432_1: pin names not known; wires that end beside it: 1'b1, n7408_1_pin3, n7408_1_pin6, n7432_1_p4, 1'b0
  LED led_2 (.in(xor_2_out));
  LED led_3 (.in(or_1_out));
  LED led_4 (.in(undriven));
endmodule
