// Logisim project sequentialcircuit.circ as structural Verilog: 1 circuit, main circuit main
module main (
  input  in_1,
  output out_2
);

  wire and_1_out, and_2_out, and_3_out, and_4_out, clock_1_out, d_ff_1_q, d_ff_1_qn, d_ff_2_q, d_ff_2_qn,
       or_1_out, or_2_out;

  and and_1 (and_1_out, ~in_1, d_ff_1_q, d_ff_2_q);  // AND_Gate
  and and_2 (and_2_out, in_1, d_ff_1_qn);
  and and_3 (and_3_out, in_1, d_ff_2_qn);
  and and_4 (and_4_out, in_1, d_ff_1_q);
  or or_1 (or_1_out, and_1_out, and_2_out, and_3_out);
  or or_2 (or_2_out, and_4_out, d_ff_2_q);
  Clock clock_1 (.out(clock_1_out));
  D_Flip_Flop d_ff_1 (.D(or_2_out), .clk(clock_1_out), .Q(d_ff_1_q), .Qn(d_ff_1_qn));  // open: preset, reset
  D_Flip_Flop d_ff_2 (.D(or_1_out), .clk(clock_1_out), .Q(d_ff_2_q), .Qn(d_ff_2_qn));  // open: preset, reset
  and and_5 (out_2, ~in_1, d_ff_1_q, d_ff_2_q);  // AND_Gate
endmodule
